# Fritzing sketch meteo (saved by Fritzing 0.9.3b)
circuit board: 10cm x 10cm
breadboards: 1

parts:
  Q1 = NPN-Transistor [package="TO92 [THT]"]
  at85 = attiny85 [package=dip]
  R1 = Resistor [tolerance=±5% resistance=220 package=THT]
  24LC32 = 24LC32 [package=THT]
  DHT22 = DHT22 Humidity and Temperature Sensor
  ESP01 = ESP8266 WiFi Module [part_number=ESP8266]
  BMP180 = BMP180 Breakout (GY-68)
  R2 = Resistor [tolerance=±10% resistance=4.7k package=THT]
  C1 = Electrolytic Capacitor [capacitance=22µF voltage=16V package="100 mil [THT, electrolytic]"]
  +_- = female pin header, 2 pins [form="♀ (female)"]

nets:
  VDD: Q1.E, 24LC32.+V, DHT22.VDD, BMP180.VCC, R2.Pin_1
  N1: Q1.B, R1.Pin_0
  N2: Q1.C, at85.Pin_8, C1.+, +_-.pin2
  N3: at85.Pin_2, DHT22.DATA, R2.Pin_0
  GND: at85.Pin_4, 24LC32.A0, 24LC32.A1, 24LC32.A2, 24LC32.0V, DHT22.GND, ESP01.GND, BMP180.GND, C1.-, +_-.pin1
  N4: at85.Pin_5, 24LC32.SDA_-_I2C_Data, ESP01.GPIO_0, BMP180.SDA
  N5: at85.Pin_6, R1.Pin_1
  N6: at85.Pin_7, 24LC32.SCL_-_I2C_Clock, ESP01.GPIO_2, BMP180.SCL
  N7: ESP01.VCC, ESP01.CH_PD

notes:
  scl
  sda
  debug

custom parts:
  ESP8266 WiFi Module: Generic WiFi Module based on the ESP8266 with onboard PCB antenna and UART communications
  BMP180 Breakout (GY-68): This is a simple breakout board for the BMP180, a high-precision, low-power barometric pressure sensor made by Bosch Sensortec. The range of measurement is from 300hPa to 1100hPa. The sensor can be supplied with voltage ranging from 1.8V to 3.6V. Operating temperature range is -40 to +85 °C. This particular breakout board (or perhaps the configuration) is produced by Shenzhen Keep Power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
