# Fritzing sketch meteo_multiple (saved by Fritzing 0.9.3b)
circuit board: 10cm x 10cm
breadboards: 1

parts:
  Q1 = NPN-Transistor [package="TO92 [THT]"]
  at85 = attiny85 [package=dip]
  R1 = Resistor [tolerance=±5% resistance=220 package=THT]
  24LC32 = 24LC32 [package=THT]
  DHT22 = DHT22 Humidity and Temperature Sensor
  ESP01 = ESP8266 WiFi Module [part_number=ESP8266]
  BMP180 = BMP180 Breakout (GY-68)
  R2 = Resistor [tolerance=±10% resistance=4.7k package=THT]
  C1 = Electrolytic Capacitor [capacitance=22µF voltage=16V package="100 mil [THT, electrolytic]"]
  +_- = female pin header, 2 pins [form="♀ (female)"]
  R3 = Resistor [tolerance=±10% resistance=4.7k package=THT]
  C2 = Electrolytic Capacitor [capacitance=22µF voltage=16V package="100 mil [THT, electrolytic]"]
  ESP2 = ESP8266 WiFi Module [part_number=ESP8266]
  BMP181 = BMP180 Breakout (GY-68)
  R4 = Resistor [tolerance=±5% resistance=220 package=THT]
  24LC33 = 24LC32 [package=THT]
  DHT23 = DHT22 Humidity and Temperature Sensor
  Q2 = NPN-Transistor [package="TO92 [THT]"]
  at86 = attiny85 [package=dip]
  +_-1 = female pin header, 2 pins [form="♀ (female)"]
  R5 = Resistor [tolerance=±10% resistance=4.7k package=THT]
  C3 = Electrolytic Capacitor [capacitance=22µF voltage=16V package="100 mil [THT, electrolytic]"]
  ESP3 = ESP8266 WiFi Module [part_number=ESP8266]
  BMP182 = BMP180 Breakout (GY-68)
  R6 = Resistor [tolerance=±5% resistance=220 package=THT]
  24LC34 = 24LC32 [package=THT]
  DHT24 = DHT22 Humidity and Temperature Sensor
  Q3 = NPN-Transistor [package="TO92 [THT]"]
  at87 = attiny85 [package=dip]
  +_-2 = female pin header, 2 pins [form="♀ (female)"]
  R7 = Resistor [tolerance=±10% resistance=4.7k package=THT]
  R8 = Resistor [tolerance=±10% resistance=4.7k package=THT]
  R9 = Resistor [tolerance=±10% resistance=4.7k package=THT]
  C4 = Electrolytic Capacitor [capacitance=22µF voltage=16V package="100 mil [THT, electrolytic]"]
  C5 = Electrolytic Capacitor [capacitance=22µF voltage=16V package="100 mil [THT, electrolytic]"]
  C6 = Electrolytic Capacitor [capacitance=22µF voltage=16V package="100 mil [THT, electrolytic]"]
  ESP4 = ESP8266 WiFi Module [part_number=ESP8266]
  ESP5 = ESP8266 WiFi Module [part_number=ESP8266]
  ESP6 = ESP8266 WiFi Module [part_number=ESP8266]
  BMP183 = BMP180 Breakout (GY-68)
  BMP184 = BMP180 Breakout (GY-68)
  BMP185 = BMP180 Breakout (GY-68)
  R10 = Resistor [tolerance=±5% resistance=220 package=THT]
  R11 = Resistor [tolerance=±5% resistance=220 package=THT]
  R12 = Resistor [tolerance=±5% resistance=220 package=THT]
  24LC35 = 24LC32 [package=THT]
  24LC36 = 24LC32 [package=THT]
  24LC37 = 24LC32 [package=THT]
  DHT25 = DHT22 Humidity and Temperature Sensor
  DHT26 = DHT22 Humidity and Temperature Sensor
  DHT27 = DHT22 Humidity and Temperature Sensor
  Q4 = NPN-Transistor [package="TO92 [THT]"]
  Q5 = NPN-Transistor [package="TO92 [THT]"]
  Q6 = NPN-Transistor [package="TO92 [THT]"]
  at88 = attiny85 [package=dip]
  at89 = attiny85 [package=dip]
  at90 = attiny85 [package=dip]
  +_-3 = female pin header, 2 pins [form="♀ (female)"]
  +_-4 = female pin header, 2 pins [form="♀ (female)"]
  +_-5 = female pin header, 2 pins [form="♀ (female)"]

nets:
  VDD: Q1.E, 24LC32.+V, DHT22.VDD, BMP180.VCC, R2.Pin_1
  N1: Q1.B, R1.Pin_0
  N2: Q1.C, at85.Pin_8, C1.+, +_-.pin2
  N3: at85.Pin_2, DHT22.DATA, R2.Pin_0
  GND: at85.Pin_4, 24LC32.A0, 24LC32.A1, 24LC32.A2, 24LC32.0V, DHT22.GND, ESP01.GND, BMP180.GND, C1.-, +_-.pin1
  N4: at85.Pin_5, 24LC32.SDA_-_I2C_Data, ESP01.GPIO_0, BMP180.SDA
  N5: at85.Pin_6, R1.Pin_1
  N6: at85.Pin_7, 24LC32.SCL_-_I2C_Clock, ESP01.GPIO_2, BMP180.SCL
  N7: ESP01.VCC, ESP01.CH_PD
  N8: R3.Pin_0, DHT23.DATA, at86.Pin_2
  VCC: R3.Pin_1, BMP181.VCC, 24LC33.+V, DHT23.VDD, Q2.E
  GND_2: C2.-, ESP2.GND, BMP181.GND, 24LC33.A0, 24LC33.A1, 24LC33.A2, 24LC33.0V, DHT23.GND, at86.Pin_4, +_-1.pin1
  N9: C2.+, Q2.C, at86.Pin_8, +_-1.pin2
  N10: ESP2.VCC, ESP2.CH_PD
  N11: ESP2.GPIO_0, BMP181.SDA, 24LC33.SDA_-_I2C_Data, at86.Pin_5
  N12: ESP2.GPIO_2, BMP181.SCL, 24LC33.SCL_-_I2C_Clock, at86.Pin_7
  N13: R4.Pin_0, Q2.B
  N14: R4.Pin_1, at86.Pin_6
  N15: R5.Pin_0, DHT24.DATA, at87.Pin_2
  VCC_2: R5.Pin_1, BMP182.VCC, 24LC34.+V, DHT24.VDD, Q3.E
  GND_3: C3.-, ESP3.GND, BMP182.GND, 24LC34.A0, 24LC34.A1, 24LC34.A2, 24LC34.0V, DHT24.GND, at87.Pin_4, +_-2.pin1
  N16: C3.+, Q3.C, at87.Pin_8, +_-2.pin2
  N17: ESP3.VCC, ESP3.CH_PD
  N18: ESP3.GPIO_0, BMP182.SDA, 24LC34.SDA_-_I2C_Data, at87.Pin_5
  N19: ESP3.GPIO_2, BMP182.SCL, 24LC34.SCL_-_I2C_Clock, at87.Pin_7
  N20: R6.Pin_0, Q3.B
  N21: R6.Pin_1, at87.Pin_6
  N22: R7.Pin_0, DHT25.DATA, at88.Pin_2
  VCC_3: R7.Pin_1, BMP183.VCC, 24LC35.+V, DHT25.VDD, Q4.E
  N23: R8.Pin_0, DHT27.DATA, at90.Pin_2
  VCC_4: R8.Pin_1, BMP185.VCC, 24LC37.+V, DHT27.VDD, Q6.E
  N24: R9.Pin_0, DHT26.DATA, at89.Pin_2
  VCC_5: R9.Pin_1, BMP184.VCC, 24LC36.+V, DHT26.VDD, Q5.E
  GND_4: C4.-, ESP4.GND, BMP183.GND, 24LC35.A0, 24LC35.A1, 24LC35.A2, 24LC35.0V, DHT25.GND, at88.Pin_4, +_-3.pin1
  N25: C4.+, Q4.C, at88.Pin_8, +_-3.pin2
  GND_5: C5.-, ESP5.GND, BMP185.GND, 24LC37.A0, 24LC37.A1, 24LC37.A2, 24LC37.0V, DHT27.GND, at90.Pin_4, +_-4.pin1
  N26: C5.+, Q6.C, at90.Pin_8, +_-4.pin2
  GND_6: C6.-, ESP6.GND, BMP184.GND, 24LC36.A0, 24LC36.A1, 24LC36.A2, 24LC36.0V, DHT26.GND, at89.Pin_4, +_-5.pin1
  N27: C6.+, Q5.C, at89.Pin_8, +_-5.pin2
  N28: ESP4.VCC, ESP4.CH_PD
  N29: ESP4.GPIO_0, BMP183.SDA, 24LC35.SDA_-_I2C_Data, at88.Pin_5
  N30: ESP4.GPIO_2, BMP183.SCL, 24LC35.SCL_-_I2C_Clock, at88.Pin_7
  N31: ESP5.VCC, ESP5.CH_PD
  N32: ESP5.GPIO_0, BMP185.SDA, 24LC37.SDA_-_I2C_Data, at90.Pin_5
  N33: ESP5.GPIO_2, BMP185.SCL, 24LC37.SCL_-_I2C_Clock, at90.Pin_7
  N34: ESP6.VCC, ESP6.CH_PD
  N35: ESP6.GPIO_0, BMP184.SDA, 24LC36.SDA_-_I2C_Data, at89.Pin_5
  N36: ESP6.GPIO_2, BMP184.SCL, 24LC36.SCL_-_I2C_Clock, at89.Pin_7
  N37: R10.Pin_0, Q4.B
  N38: R10.Pin_1, at88.Pin_6
  N39: R11.Pin_0, Q5.B
  N40: R11.Pin_1, at89.Pin_6
  N41: R12.Pin_0, Q6.B
  N42: R12.Pin_1, at90.Pin_6

notes:
  scl
  sda
  debug

custom parts:
  ESP8266 WiFi Module: Generic WiFi Module based on the ESP8266 with onboard PCB antenna and UART communications
  BMP180 Breakout (GY-68): This is a simple breakout board for the BMP180, a high-precision, low-power barometric pressure sensor made by Bosch Sensortec. The range of measurement is from 300hPa to 1100hPa. The sensor can be supplied with voltage ranging from 1.8V to 3.6V. Operating temperature range is -40 to +85 °C. This particular breakout board (or perhaps the configuration) is produced by Shenzhen Keep Power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
